# Fritzing sketch pi_cam_circuit (saved by Fritzing 0.8.5b)
stripboards: 1

parts:
  Raspberry_Pi_B_rev1 = Raspberry Pi B rev2
  R2 = Resistor [tolerance=±5% resistance=560 package="1206 [SMD]"]
  R3 = Resistor [tolerance=±5% resistance=560 package="1206 [SMD]"]
  R4 = Resistor [tolerance=±5% resistance=560 package="1206 [SMD]"]  # not connected
  LED1 = LED - 5mm [color="Red (633nm)" package="5 mm [THT]"]
  LED3 = LED - 5mm [color="Yellow (585nm)" package="5 mm [THT]"]
  LED2 = LED - 5mm [color="Green (555nm)" package="5 mm [THT]"]
  S1 = Round Pushbutton

nets:
  N1: Raspberry_Pi_B_rev1.GPIO_2, S1.leg0
  N2: Raspberry_Pi_B_rev1.GND, R2.Pin_0, R3.Pin_0, S1.leg1
  N3: Raspberry_Pi_B_rev1.GPIO_17, LED3.anode
  N4: Raspberry_Pi_B_rev1.GPIO_18, LED2.anode
  N5: Raspberry_Pi_B_rev1.GPIO_27, LED1.anode
  N6: R2.Pin_1, LED2.cathode
  N7: R3.Pin_1, LED1.cathode
